# Fritzing sketch new-schema (saved by Fritzing 1.0.6)
breadboards: 1

parts:
  S1 = Pushbutton [package="[THT]"]
  A1 = Arduino Nano 33 BLE Sense
  OLED1 = SSD1306 0.96in 128x64 I2C Monochrome OLED Display
  A2 = Seeed wio-e5

nets:
  N1: S1.Pin_1, S1.Pin_2, A1.Pin_14, A1.Pin_19, OLED1.GND, A2.Pin_2
  N2: S1.Pin_3, S1.Pin_4, A1.Pin_20
  N3: A1.Pin_2, OLED1.VCC, A2.Pin_1
  N4: A1.Pin_8, OLED1.SDA
  N5: A1.Pin_9, OLED1.SCL
  N6: A1.Pin_13, A1.Pin_18
  N7: A1.Pin_16, A2.Pin_3
  N8: A1.Pin_17, A2.Pin_4

custom parts:
  Arduino Nano 33 BLE Sense: The Nano 33 BLE Sense (without headers) is Arduino’s 3.3V AI enabled board in the smallest available form factor: 45x18mm! The Arduino Nano 33 BLE Sense is a completely new board on a well-known form factor. It comes with a series of embedded sensors: 9 axis inertial sensor: what makes this board ideal for wearable devices humidity, and temperature sensor: to get highly accurate measurements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
  Seeed wio-e5: text
